# Fritzing sketch Assignment 1 (saved by Fritzing 0.9.3b)
breadboards: 1

parts:
  U1 = ESP8266 NodeMCU LoLin module
  DHT1 = Humidity and Temperature Sensor DHT11
  OLED_I2C1 = OLED 128x64 I2C Monochrome Display

nets:
  N1: U1.D5, DHT1.Data-signal
  VCC: DHT1.Vcc, DHT1.GND_1, DHT1.GND_2, OLED_I2C1.VDD

custom parts:
  ESP8266 NodeMCU LoLin module: ESP8266 based NodeMCU
  Humidity and Temperature Sensor DHT11: Digital relative humidity & temperature sensor DHT11
